# Fritzing sketch Wiring (saved by Fritzing 0.9.2b)
circuit board: 5.64444cm x 8.46667cm
breadboards: 1
perfboards: 1

parts:
  R1 = Resistor [tolerance=±5% resistance=4.7k package=THT]
  RHT1 = Humidity and Temperature Sensor RHT03
  Light_Sensor = Photocell (LDR) [package=THT]
  R2 = Resistor [tolerance=±5% resistance=4.7k package=THT]
  U1 = TEMPERATURE-SENSOR [package=to-92]
  R3 = Resistor [tolerance=±5% resistance=4.7k package=THT]
  Arduino_Yun = Arduino Yun

nets:
  VCC: R1.Pin_0, RHT1.Vcc, Light_Sensor.pin_0, R2.Pin_0, U1.VCC, R3.Pin_1, Arduino_Yun.5V
  N1: R1.Pin_1, RHT1.Data-signal, Arduino_Yun.D2/SDA, Arduino_Yun.D2
  N2: RHT1.GND_2, U1.ADJ, Arduino_Yun.GND
  N3: Light_Sensor.pin_1, R2.Pin_1, Arduino_Yun.A0
  N4: U1.GND, R3.Pin_0, Arduino_Yun.D10_PWM/SS
